# Fritzing sketch Connection Diagram (saved by Fritzing 1.0.5)

parts:
  A1 = XIAO ESP32C3-tht
  Part1 = LCD1602-I2C

nets:
  N1: A1.Pin_2, A1.Pin_21, Part1.GND
  N2: A1.Pin_13, Part1.SDA
  N3: A1.Pin_14, Part1.SCL
  N4: A1.Pin_22, Part1.VCC

custom parts:
  XIAO ESP32C3-tht: Seeed Studio XIAO ESP32C3 adopts new RISC-V architecture, supporting both Wi-Fi and BLE wireless connectivities.
  LCD1602-I2C: A standard character display, usually with 2x16 characters. Comes in many colors with LCM1602 IIC attached.
